# Fritzing sketch photosense (saved by Fritzing 0.6.3b)
breadboards: 1

parts:
  Arduino1 = Arduino
  R1 = Resistor [tolerance=±5% resistance=1k package=THT]
  D1 = Rectifier Diode [part_number=1N4001 package="300 mil [THT]"]
  Q1 = NPN-Transistor [package="TO92 [THT]"]

nets:
  N1: Arduino1.GND, Q1.E
  N2: Arduino1.D12, D1.anode, Q1.C
  N3: Arduino1.+5V, R1.Pin_0
  N4: R1.Pin_1, D1.cathode
